// Digital circuit Alu.dig as structural Verilog
module Alu (
  input  [31:0] A,
  input  [31:0] B,
  input  [3:0] C,
  output [31:0] Y
);

  wire bitcount_1_out, bitcount_2_out;
  wire [31:0] add_1_s, and_1_out, barrelshifter_1_out, barrelshifter_2_out, demultiplexer_1_out_0,
       demultiplexer_1_out_1, demultiplexer_1_out_2, demultiplexer_1_out_3, demultiplexer_1_out_4,
       demultiplexer_1_out_5, demultiplexer_1_out_6, demultiplexer_2_out_0, demultiplexer_2_out_1,
       demultiplexer_2_out_2, demultiplexer_2_out_3, demultiplexer_2_out_4, demultiplexer_2_out_5,
       demultiplexer_2_out_6, or_1_out, sub_1_s, xor_1_out;

  Demultiplexer #(.Selector_Bits(4), .Bits(32)) demultiplexer_1 (
    .sel(C), .in(A), .out_0(demultiplexer_1_out_0), .out_1(demultiplexer_1_out_1),
    .out_2(demultiplexer_1_out_2), .out_3(demultiplexer_1_out_3), .out_4(demultiplexer_1_out_4),
    .out_5(demultiplexer_1_out_5), .out_6(demultiplexer_1_out_6));  // open: out_7, out_8, out_9, out_10, out_11, out_12, out_13, out_14, out_15
  Demultiplexer #(.Selector_Bits(4), .Bits(32)) demultiplexer_2 (
    .sel(C), .in(B), .out_0(demultiplexer_2_out_0), .out_1(demultiplexer_2_out_1),
    .out_2(demultiplexer_2_out_2), .out_3(demultiplexer_2_out_3), .out_4(demultiplexer_2_out_4),
    .out_5(demultiplexer_2_out_5), .out_6(demultiplexer_2_out_6));  // open: out_7, out_8, out_9, out_10, out_11, out_12, out_13, out_14, out_15
  BitCount #(.Bits(32)) bitcount_1 (.in(demultiplexer_2_out_4), .out(bitcount_1_out));
  BitCount #(.Bits(32)) bitcount_2 (.in(demultiplexer_2_out_5), .out(bitcount_2_out));
  Add #(.Bits(32)) add_1 (.a(demultiplexer_1_out_2), .b(demultiplexer_2_out_2), .c_i(1'b0), .s(add_1_s));  // open: c_o
  Sub #(.Bits(32)) sub_1 (.a(demultiplexer_1_out_6), .b(demultiplexer_2_out_6), .c_i(1'b0), .s(sub_1_s));  // open: c_o
  assign and_1_out = demultiplexer_1_out_0 & demultiplexer_2_out_0;  // And and_1, 32 bits wide
  assign or_1_out = demultiplexer_1_out_1 | demultiplexer_2_out_1;  // Or or_1, 32 bits wide
  assign xor_1_out = demultiplexer_1_out_3 ^ demultiplexer_2_out_3;  // XOr xor_1, 32 bits wide
  BarrelShifter #(.Bits(32)) barrelshifter_1 (
    .in(demultiplexer_1_out_4), .shift(bitcount_1_out), .out(barrelshifter_1_out));
  BarrelShifter #(.Bits(32), .direction("right")) barrelshifter_2 (
    .in(demultiplexer_1_out_5), .shift(bitcount_2_out), .out(barrelshifter_2_out));
  Multiplexer #(.Selector_Bits(4), .Bits(32)) multiplexer_1 (
    .sel(C), .in_0(and_1_out), .in_1(or_1_out), .in_2(add_1_s), .in_3(xor_1_out), .in_4(barrelshifter_1_out),
    .in_5(barrelshifter_2_out), .in_6(sub_1_s), .in_7({32{1'b0}}), .in_8({32{1'b0}}), .in_9({32{1'b0}}),
    .in_10({32{1'b0}}), .in_11({32{1'b0}}), .in_12({32{1'b0}}), .in_13({32{1'b0}}), .in_14({32{1'b0}}),
    .in_15({32{1'b0}}), .out(Y));

  // Notes on the sheet:
  //   A: A
  //   0000-AND
  //   0001-OR
  //   0010-ADD
  //   0011-XOR
  //   0100-Shift left
  //   0101-Shift right
  //   0110-SUB
endmodule
