// Digital circuit CPU2.dig as structural Verilog
module CPU2 (
  input  clk,
  input  in_3,
  input  [31:0] in_7,
  input  jump_i,
  input  [31:0] jump_pc,
  output [6:0] out_1,
  output [4:0] out_4,
  output [4:0] out_5,
  output [4:0] out_6,
  output [31:0] out_8,
  output [1:0] out_9,
  output out_10,
  output out_11,
  output out_12,
  output out_13,
  output out_14,
  output out_15,
  output out_16,
  output [31:0] pc_o
);

  wire button_1_out;
  wire [23:0] blocoif_1_inst_addr;
  wire [31:0] blocoif_1_pc_o, inst_memory_d, u_IFID_inst_o, u_register_file_rs1_data,
       u_register_file_rs2_data;

  Button button_1 (.out(button_1_out));
  blocoIF blocoif_1 (
    .jump(jump_i), .jump_pc(jump_pc), .clk(clk), .reset(button_1_out), .inst_addr(blocoif_1_inst_addr),
    .pc_o(blocoif_1_pc_o));
  ROM #(.AddrBits(24), .Bits(32)) inst_memory (.A(blocoif_1_inst_addr), .sel(1'b1), .D(inst_memory_d));
  IFID #(.applicationType("GHDL")) u_IFID (
    .pc_i(blocoif_1_pc_o), .inst_i(inst_memory_d), .clk(clk), .reset(button_1_out), .pc_o(pc_o),
    .inst_o(u_IFID_inst_o));
  instruction_parser #(.applicationType("GHDL")) u_instruction_parser (
    .instruction_i(u_IFID_inst_o), .opcode_o(out_1), .rd_o(out_6), .rs1_o(out_4), .rs2_o(out_5));
  register_file #(.applicationType("GHDL")) u_register_file (
    .clk(clk), .reset(button_1_out), .reg_write(in_3), .rs1_addr(out_4), .rs2_addr(out_5), .rd_addr(out_6),
    .rd_data(in_7), .rs1_data(u_register_file_rs1_data), .rs2_data(u_register_file_rs2_data));
  immediate_extractor #(.applicationType("GHDL")) u_immediate_extractor (
    .instruction_i(u_IFID_inst_o), .immediate_o(out_8));
  control_unit #(.applicationType("GHDL")) u_control_unit (
    .opcode(out_1), .alu_op(out_9), .alu_src(out_10), .mem_read(out_11), .mem_write(out_12),
    .mem_to_reg(out_13), .reg_write(out_14), .branch(out_15), .jump(out_16));
  ID_EX_Pipeline #(.applicationType("GHDL")) u_ID_EX_Pipeline (
    .clk(clk), .reset(button_1_out), .ALUOp_in(out_9), .ALUSrc_in(out_10), .memRead_in(out_11),
    .memWrite_in(out_12), .memToReg_in(out_13), .regWrite_in(out_14), .branch_in(out_15), .jump_in(out_16),
    .Rs1_data_in(u_register_file_rs1_data), .Rs2_data_in(u_register_file_rs2_data), .Imm_in(out_8),
    .Rs1_in(out_4), .Rs2_in(out_5), .Rd_in(out_6));  // open: ALUOp_out, ALUSrc_out, memRead_out, memWrite_out, memToReg_out, regWrite_out, branch_out, jump_out, Rs1_data_out, Rs2_data_out, Imm_out, Rs1_out, Rs2_out, Rd_out

  // Notes on the sheet:
  //   jump_pc: Valor de pc para o qual devemos dar jump
  //   pc_o: Saída PC do registrador IF/ID
  //   Estágio IF
endmodule

/* Code of IFID:
-- Registrador que guarda os dados necessários entre IF e ID. Esses dados são o valor de PC e a instrução da vez
library IEEE;
use IEEE.STD_LOGIC_1164.ALL;

entity IFID is
	Port (
    	pc_i : in std_logic_vector(31 downto 0);
        inst_i: in std_logic_vector(31 downto 0);

    	clk: in std_logic;
        reset: in std_logic;

        pc_o: out std_logic_vector(31 downto 0);
        inst_o: out std_logic_vector(31 downto 0)
    	);
end IFID;

architecture Behavioral of IFID is

begin

process(clk, reset)
begin
	if reset = '1' then
        pc_o <= X"00000000";
        inst_o <= X"00000000";
	else
		if clk'event and clk = '1' then
			pc_o <= pc_i;
            inst_o <= inst_i;
		end if;
	end if;
end process;

end Behavioral;
*/

/* Code of instruction_parser:
library ieee;
use ieee.std_logic_1164.all;

entity instruction_parser is
    port (
        instruction_i : in  std_logic_vector(31 downto 0); -- 32-bit RISC-V instruction

        -- Extracted fields
        opcode_o      : out std_logic_vector(6 downto 0);  -- bits 6-0
        rd_o          : out std_logic_vector(4 downto 0);  -- bits 11-7
        rs1_o         : out std_logic_vector(4 downto 0);  -- bits 19-15
        rs2_o         : out std_logic_vector(4 downto 0)  -- bits 24-20
    );
end entity instruction_parser;

architecture behavioral of instruction_parser is
begin

    -- Simple direct assignments for common fields
    opcode_o <= instruction_i(6 downto 0);
    rd_o     <= instruction_i(11 downto 7);
    rs1_o    <= instruction_i(19 downto 15);
    rs2_o    <= instruction_i(24 downto 20);

end architecture behavioral;
*/

/* Code of register_file:
library ieee;
use ieee.std_logic_1164.all;
use ieee.numeric_std.all;

entity register_file is
    port (
        clk      : in  std_logic;
        reset    : in  std_logic;
        reg_write: in  std_logic; -- Control signal to enable writing
        rs1_addr : in  std_logic_vector(4 downto 0);
        rs2_addr : in  std_logic_vector(4 downto 0);
        rd_addr  : in  std_logic_vector(4 downto 0);
        rd_data  : in  std_logic_vector(31 downto 0);
        rs1_data : out std_logic_vector(31 downto 0);
        rs2_data : out std_logic_vector(31 downto 0)
    );
end entity register_file;

architecture behavioral of register_file is
    -- Define the storage for 32 registers, each 32 bits wide
    type reg_array is array (0 to 31) of std_logic_vector(31 downto 0);
    signal registers : reg_array := (others => (others => '0'));

begin

    -- Reset Process: Asynchronous reset to clear all registers
    reset_proc: process(reset)
    begin
        if reset = '1' then
            -- Clear all registers to zero on reset
            for i in 0 to 31 loop
                registers(i) <= (others => '0');
            end loop;
        end if;
    end process reset_proc;

    -- Read Process: Synchronous to the rising edge (first half of the clock)
    read_proc: process(clk)
    begin
        if rising_edge(clk) then
            -- Read rs1. Reading x0 always returns zero.
            if rs1_addr = "00000" then
                rs1_data <= (others => '0');
            else
                rs1_data <= registers(to_integer(unsigned(rs1_addr)));
            end if;

            -- Read rs2. Reading x0 always returns zero.
            if rs2_addr = "00000" then
                rs2_data <= (others => '0');
            else
                rs2_data <= registers(to_integer(unsigned(rs2_addr)));
            end if;
        end if;
    end process read_proc;

    -- Write Process: Synchronous to the falling edge (second half of the clock)
    write_proc: process(clk)
    begin
        if falling_edge(clk) then
            -- Write only if reg_write is enabled and the destination is not x0
            if reg_write = '1' and rd_addr /= "00000" then
                registers(to_integer(unsigned(rd_addr))) <= rd_data;
            end if;
        end if;
    end process write_proc;

end architecture behavioral;
*/

/* Code of immediate_extractor:
library ieee;
use ieee.std_logic_1164.all;
use ieee.numeric_std.all; -- For signed arithmetic and type conversions

entity immediate_extractor is
    port (
        instruction_i : in  std_logic_vector(31 downto 0); -- 32-bit RISC-V instruction input
        immediate_o   : out std_logic_vector(31 downto 0)  -- 32-bit sign-extended immediate output
    );
end entity immediate_extractor;

architecture behavioral of immediate_extractor is
    -- Internal signal to hold the opcode (bits 6 downto 0) for use in the process.
    signal opcode_s : std_logic_vector(6 downto 0);
begin

    -- Extract the opcode from the instruction. This assignment is concurrent.
    opcode_s <= instruction_i(6 downto 0);

    -- This process block implements the combinational logic for immediate extraction.
    -- The sensitivity list includes all signals that, when changed, should
    -- re-evaluate the logic inside the process.
    process(instruction_i, opcode_s)
        -- Declare a local variable to build the immediate value before assigning it
        -- to the output signal. Variables are evaluated immediately within the process.
        variable imm : std_logic_vector(31 downto 0);
    begin
        -- Use a case statement to select the immediate extraction logic
        -- based on the instruction's opcode.
        case opcode_s is
            -- I-type immediate (Load, Op-Imm, JALR)
            -- Opcode values: 0x03 (LOAD), 0x13 (OP-IMM), 0x67 (JALR)
            -- Format: imm[11:0] is instruction[31:20]
            when "0000011" | "0010011" | "1100111" =>
                -- Sign-extend the 12-bit immediate: replicate bit 31 of the instruction
                -- (which is imm[11]) across the higher bits (31 downto 12) of the 32-bit immediate.
                imm := (others => instruction_i(31));
                -- Place the 12-bit immediate into the lower 12 bits of 'imm'.
                imm(11 downto 0) := instruction_i(31 downto 20);
                -- Assign the constructed immediate to the output.
                immediate_o <= imm;

            -- S-type immediate (Store)
            -- Opcode value: 0x23 (STORE)
            -- Format: imm[11:5] from instruction[31:25], imm[4:0] from instruction[11:7]
            -- Reconstructed: imm[11:5] << 5 | imm[4:0]
            when "0100011" =>
                -- Sign-extend the 12-bit immediate: use bit 31 of the instruction
                -- (which is imm[11]) for sign extension.
                imm := (others => instruction_i(31));
                -- Place the high part of the immediate (imm[11:5]) into its position.
                imm(11 downto 5) := instruction_i(31 downto 25);
                -- Place the low part of the immediate (imm[4:0]) into its position.
                imm(4 downto 0)  := instruction_i(11 downto 7);
                -- Assign the constructed immediate to the output.
                immediate_o <= imm;

            -- B-type immediate (Branch)
            -- Opcode value: 0x63 (BRANCH)
            -- Format: imm[12|10:5|4:1|11]
            -- Bits: instruction[31] (imm[12]), instruction[30:25] (imm[10:5]),
            --       instruction[11:8] (imm[4:1]), instruction[7] (imm[11])
            -- Reconstructed: imm[12] << 12 | imm[11] << 11 | imm[10:5] << 5 | imm[4:1] << 1 (imm[0] is always '0')
            when "1100011" =>
                -- Sign-extend the 13-bit immediate: use bit 31 of the instruction
                -- (which is imm[12]) for sign extension.
                imm := (others => instruction_i(31));
                -- Place fragmented immediate bits into their correct positions.
                imm(12)        := instruction_i(31);         -- imm[12]
                imm(11)        := instruction_i(7);          -- imm[11]
                imm(10 downto 5) := instruction_i(30 downto 25); -- imm[10:5]
                imm(4 downto 1) := instruction_i(11 downto 8);  -- imm[4:1]
                imm(0)         := '0';                       -- imm[0] is always 0 for branches
                -- Assign the constructed immediate to the output.
                immediate_o <= imm;

            -- U-type immediate (LUI, AUIPC)
            -- Opcode values: 0x37 (LUI), 0x17 (AUIPC)
            -- Format: imm[31:12] is instruction[31:12]
            -- This immediate is already effectively shifted left by 12 bits.
            when "0110111" | "0010111" =>
                -- Concatenate the upper 20 bits of the instruction with 12 zeros.
                -- No explicit sign extension needed, as the value is simply the upper bits.
                imm := instruction_i(31 downto 12) & (11 downto 0 => '0');
                -- Assign the constructed immediate to the output.
                immediate_o <= imm;

            -- J-type immediate (JAL)
            -- Opcode value: 0x6F (JAL)
            -- Format: imm[20|10:1|11|19:12]
            -- Bits: instruction[31] (imm[20]), instruction[19:12] (imm[19:12]),
            --       instruction[20] (imm[11]), instruction[30:21] (imm[10:1])
            -- Reconstructed: imm[20] << 20 | imm[19:12] << 12 | imm[11] << 11 | imm[10:1] << 1 (imm[0] is always '0')
            when "1101111" =>
                -- Sign-extend the 21-bit immediate: use bit 31 of the instruction
                -- (which is imm[20]) for sign extension.
                imm := (others => instruction_i(31));
                -- Place fragmented immediate bits into their correct positions.
                imm(20)        := instruction_i(31);         -- imm[20]
                imm(19 downto 12) := instruction_i(19 downto 12); -- imm[19:12]
                imm(11)        := instruction_i(20);         -- imm[11]
                imm(10 downto 1) := instruction_i(30 downto 21); -- imm[10:1]
                imm(0)         := '0';                       -- imm[0] is always 0 for jumps
                -- Assign the constructed immediate to the output.
                immediate_o <= imm;

            -- Default case: For unrecognized opcodes, output all zeros.
            when others =>
                imm := (others => '0');
                immediate_o <= imm;
        end case;
    end process;

end architecture behavioral;
*/

/* Code of control_unit:
library ieee;
use ieee.std_logic_1164.all;

entity control_unit is
    port (
        -- Inputs
        opcode      : in  std_logic_vector(6 downto 0); -- 7-bit opcode from the instruction

        -- Outputs: Control signals for the datapath
        alu_op      : out std_logic_vector(1 downto 0); -- Controls the ALU's main operation:
                                                  -- "00" = Add (for Loads/Stores/AUIPC/LUI/JAL/JALR address calc or pass-through)
                                                  -- "01" = Subtract (for Branches for comparison)
                                                  -- "10" = R-type operation (further decoded by funct3/funct7)
                                                  -- "11" = I-type operation (further decoded by funct3)
        alu_src     : out std_logic;              -- Selects the second ALU source:
                                                  -- '0' = rs2 data (for R-type)
                                                  -- '1' = immediate (for I, S, B, U, J-types)
        mem_read    : out std_logic;              -- Enables reading from data memory
        mem_write   : out std_logic;              -- Enables writing to data memory
        mem_to_reg  : out std_logic;              -- Selects if data from memory goes to the register file (for loads)
        reg_write   : out std_logic;              -- Enable writing to the register file
        branch      : out std_logic;              -- Indicates a conditional branch instruction
        jump        : out std_logic              -- Indicates an unconditional jump instruction (JAL, JALR)

    );
end entity control_unit;

architecture behavioral of control_unit is
    -- Define the opcodes for different instruction types as constants for readability
    constant R_TYPE_OP   : std_logic_vector(6 downto 0) := "0110011"; -- OP (e.g., ADD, SUB, AND, OR, XOR)
    constant I_TYPE_OP   : std_logic_vector(6 downto 0) := "0010011"; -- OP-IMM (e.g., ADDI, ANDI, ORI)
    constant L_TYPE_OP   : std_logic_vector(6 downto 0) := "0000011"; -- LOAD (e.g., LW)
    constant S_TYPE_OP   : std_logic_vector(6 downto 0) := "0100011"; -- STORE (e.g., SW)
    constant B_TYPE_OP   : std_logic_vector(6 downto 0) := "1100011"; -- BRANCH (e.g., BEQ, BNE)
    constant JAL_OP      : std_logic_vector(6 downto 0) := "1101111"; -- JAL (Jump and Link)
    constant JALR_OP     : std_logic_vector(6 downto 0) := "1100111"; -- JALR (Jump and Link Register)
    constant LUI_OP      : std_logic_vector(6 downto 0) := "0110111"; -- LUI (Load Upper Immediate)
    constant AUIPC_OP    : std_logic_vector(6 downto 0) := "0010111"; -- AUIPC (Add Upper Immediate to PC)

begin

    -- Main control logic process.
    -- This process is sensitive to both 'reset' and 'opcode'.
    -- All output signals must be assigned within this single process to avoid latches.
    process(opcode)
    begin
        -- safe default (e.g., NOP-like behavior, no writes, no branches/jumps).
        reg_write  <= '0';
        mem_to_reg <= '0';
        mem_read   <= '0';
        mem_write  <= '0';
        alu_src    <= '0';
        branch     <= '0';
        jump       <= '0';
        alu_op     <= "00"; -- Default to "00" (Add/Pass-through) for ALU

        -- Use a case statement to decode the opcode and assert specific control signals.
        case opcode is
            -- R-Type instructions (e.g., ADD, SUB, AND, OR)
            -- Perform register-to-register operations, write result back to register file.
            when R_TYPE_OP =>
                reg_write  <= '1';     -- Enable write to register file
                alu_src    <= '0';     -- Second ALU operand comes from rs2 (register value)
                alu_op     <= "10";    -- ALU performs R-type specific operation (decoded by ALU Control)

            -- I-Type instructions (Arithmetic/Logical with Immediate, excluding Loads/JALR)
            -- (e.g., ADDI, ANDI, ORI)
            -- Perform operation with immediate, write result back to register file.
            when I_TYPE_OP =>
                reg_write  <= '1';     -- Enable write to register file
                alu_src    <= '1';     -- Second ALU operand comes from immediate
                alu_op     <= "11";    -- ALU performs I-type specific operation (decoded by ALU Control)

            -- Load instructions (I-type, e.g., LW)
            -- Calculate memory address using immediate, read from memory, write to register file.
            when L_TYPE_OP =>
                reg_write  <= '1';     -- Enable write to register file
                mem_to_reg <= '1';     -- Data from memory is written to reg file
                mem_read   <= '1';     -- Enable memory read
                alu_src    <= '1';     -- Second ALU operand is immediate (for address calculation)
                alu_op     <= "00";    -- ALU performs addition (base register + immediate offset)

            -- Store instructions (S-type, e.g., SW)
            -- Calculate memory address using immediate, write to memory.
            when S_TYPE_OP =>
                mem_write  <= '1';     -- Enable memory write
                alu_src    <= '1';     -- Second ALU operand is immediate (for address calculation)
                alu_op     <= "00";    -- ALU performs addition (base register + immediate offset)

            -- Branch instructions (B-type, e.g., BEQ, BNE)
            -- Compare two registers, enable branch if condition met.
            when B_TYPE_OP =>
                branch     <= '1';     -- Indicate a branch instruction
                alu_op     <= "01";    -- ALU performs subtraction (for comparison)

            -- LUI (Load Upper Immediate)
            -- Loads a 20-bit immediate into the upper 20 bits of a register, clearing lower 12.
            when LUI_OP =>
                reg_write  <= '1';     -- Enable write to register file
                alu_src    <= '1';     -- Immediate is used by ALU (often conceptually for a pass-through or add 0)
                alu_op     <= "00";    -- ALU performs addition (effectively passes the immediate)

            -- AUIPC (Add Upper Immediate to PC)
            -- Adds a 20-bit immediate (shifted) to the PC, writes to register.
            when AUIPC_OP =>
                reg_write  <= '1';     -- Enable write to register file
                alu_src    <= '1';     -- Immediate is used by ALU
                alu_op     <= "00";    -- ALU performs addition (PC + immediate)

            -- JAL (Jump and Link)
            -- Unconditional jump, saves PC+4 to rd.
            when JAL_OP =>
                reg_write  <= '1';     -- Enable write to register file (for PC+4)
                jump       <= '1';     -- Indicate an unconditional jump
                alu_op     <= "00";    -- ALU may be used to calculate target address (PC + immediate) or pass PC+4

            -- JALR (Jump and Link Register)
            -- Unconditional jump to (rs1 + immediate), saves PC+4 to rd.
            when JALR_OP =>
                reg_write  <= '1';     -- Enable write to register file (for PC+4)
                jump       <= '1';     -- Indicate an unconditional jump
                alu_src    <= '1';     -- Immediate is used by ALU (for address calculation)
                alu_op     <= "00";    -- ALU performs addition (rs1 + immediate)

            -- Default case for any other undefined or unsupported opcodes.
            -- All control signals remain in their default inactive state.
            when others =>
                null; -- Explicitly do nothing, as defaults are set above.
        end case;
    end process;

end architecture behavioral;
*/

/* Code of ID_EX_Pipeline:
library IEEE;
use IEEE.STD_LOGIC_1164.ALL;
use IEEE.NUMERIC_STD.ALL;

entity ID_EX_Pipeline is
    Port (
        clk           : in  std_logic;
        reset         : in  std_logic;
        -- Control signals
        ALUOp_in      : in  std_logic_vector(1 downto 0);
        ALUSrc_in     : in  std_logic;
        memRead_in   : in  std_logic;
        memWrite_in  : in  std_logic;
        memToReg_in  : in  std_logic;
        regWrite_in  : in  std_logic;
        branch_in    : in  std_logic;
        jump_in      : in  std_logic;
        -- Data signals
        Rs1_data_in  : in  std_logic_vector(31 downto 0);
        Rs2_data_in  : in  std_logic_vector(31 downto 0);
        Imm_in : in  std_logic_vector(31 downto 0);
        Rs1_in         : in  std_logic_vector(4 downto 0);
        Rs2_in         : in  std_logic_vector(4 downto 0); 
        Rd_in         : in  std_logic_vector(4 downto 0);
        
        -- Control outputs
        ALUOp_out     : out std_logic_vector(1 downto 0);
        ALUSrc_out    : out std_logic;
        memRead_out   : out std_logic;
        memWrite_out  : out std_logic;
        memToReg_out  : out std_logic;
        regWrite_out  : out std_logic;
        branch_out    : out std_logic;
        jump_out      : out std_logic;
        -- Data outputs
        Rs1_data_out       : out std_logic_vector(31 downto 0);
        Rs2_data_out       : out std_logic_vector(31 downto 0);
        Imm_out       : out std_logic_vector(31 downto 0);
        Rs1_out       : out std_logic_vector(4 downto 0);
        Rs2_out       : out std_logic_vector(4 downto 0);
        Rd_out        : out std_logic_vector(4 downto 0)
    );
end ID_EX_Pipeline;

architecture Behavioral of ID_EX_Pipeline is
begin
    process(clk, reset)
    begin
        if reset = '1' then
            -- On reset, clear all outputs
            ALUOp_out      <= (others => '0');
            ALUSrc_out     <= '0';
            memRead_out    <= '0';
            memWrite_out   <= '0';
            memToReg_out   <= '0';
            regWrite_out   <= '0';
            branch_out     <= '0';
            jump_out       <= '0';
            Rs1_data_out       <= (others => '0');
            Rs2_data_out       <= (others => '0');
            Imm_out       <= (others => '0');
            Rs1_out         <= (others => '0');
            Rs2_out         <= (others => '0');
            Rd_out         <= (others => '0');
        elsif rising_edge(clk) then
            -- On clock edge, latch inputs to outputs
            ALUOp_out      <= ALUOp_in;
            ALUSrc_out     <= ALUSrc_in;
            memRead_out    <= memRead_in;
            memWrite_out   <= memWrite_in;
            memToReg_out   <= memToReg_in;
            regWrite_out   <= regWrite_in;
            branch_out     <= branch_in;
            jump_out       <= jump_in;
            Rs1_data_out       <= Rs1_data_in;
            Rs2_data_out       <= Rs2_data_in;
            Imm_out       <= Imm_in;
            Rs1_out         <= Rs1_in;
            Rs2_out         <= Rs2_in;
            Rd_out         <= Rd_in;
        end if;
    end process;
end Behavioral;
*/
