// Digital circuit blocoIF.dig as structural Verilog
module blocoIF (
  input  jump,
  input  [31:0] jump_pc,
  input  clk,
  input  reset,
  output [23:0] inst_addr,
  output [31:0] pc_o
);

  wire [31:0] adder_1_p3, multiplexer_1_out;

  Multiplexer #(.Bits(32)) multiplexer_1 (.sel(jump), .in_0(adder_1_p3), .in_1(jump_pc), .out(multiplexer_1_out));
  pc #(.applicationType("GHDL")) u_pc (.pc_i(multiplexer_1_out), .clk(clk), .reset(reset), .pc_o(pc_o));
  // adder adder_1: pin names not known; wires that end beside it: 32'h4, pc_o, adder_1_p3
  pc_to_addr #(.applicationType("GHDL")) u_pc_to_addr (.pc_i(pc_o), .addr_o(inst_addr));

  // Notes on the sheet:
  //   jump_pc: Valor do PC para o qual devemos dar jump
  //   pc_o: Valor interno de PC
endmodule

/* Code of pc:
-- Registrador de 32 bits com entradas PCin, clk, reset e saída PCout

library IEEE;
use IEEE.STD_LOGIC_1164.ALL;

entity pc is
	Port (
    	pc_i : in std_logic_vector(31 downto 0);
    	clk: in std_logic;
        reset: in std_logic;

        pc_o: out std_logic_vector(31 downto 0)
    	);
end pc;

architecture Behavioral of pc is

begin

process(clk, reset)
begin
	if reset = '1' then pc_o <= X"00000000";
	else
		if clk'event and clk = '1' then
			pc_o <= pc_i;
		end if;
	end if;
end process;

end Behavioral;
*/

/* Code of pc_to_addr:
-- Recebe pc(31 downto 0) e retorna pc(25 downto 2), para ser usado como endereco da memória de instrução.

-- Isso ocorre porque a memória de instrução do Digital só recebe 24 bits de endereço. Para facilitar ao máximo a gente editar a memória de instrução e fazer testes, vou configurar a memória de instrução com 24 bits de endereço e 32 bits por palavra.
-- Como os últimos 2 bits de PC são ignorados, quando somamos PC+4, estamos indo para a próxima palavra de 32 bits da memória de instrução.

library IEEE;
use IEEE.STD_LOGIC_1164.ALL;

entity pc_to_addr is
	Port (
    	pc_i : in std_logic_vector(31 downto 0);
    	
        addr_o: out std_logic_vector(23 downto 0)
    	);
end pc_to_addr;

architecture Behavioral of pc_to_addr is

begin

process(pc_i)
begin
    addr_o <= pc_i(25 downto 2);
end process;

end Behavioral;
*/
