// Digital circuit estagioIF.dig as structural Verilog
module estagioIF (
  input  jump_i,
  input  [31:0] jump_pc,
  input  clk,
  input  reset,
  output [31:0] pc_o,
  output [31:0] inst_o
);

  wire [23:0] bloco_1_inst_addr;
  wire [31:0] inst_memory_d;

  bloco bloco_1 (
    .jump(jump_i), .jump_pc(jump_pc), .clk(clk), .reset(reset), .inst_i(inst_memory_d),
    .inst_addr(bloco_1_inst_addr), .pc_o(pc_o), .inst_o(inst_o));
  ROM #(.AddrBits(24), .Bits(32)) inst_memory (.A(bloco_1_inst_addr), .sel(1'b1), .D(inst_memory_d));

  // Notes on the sheet:
  //   jump_pc: Valor de pc para o qual devemos dar jump
  //   pc_o: Valor de PC no registrador IF/ID, carregado para o restante da pipeline
  //   inst_o: Valor da instrução no registrador IF/ID, carregado para o restante da pipeline
endmodule
