// Digital circuit Estágio_EX.dig as structural Verilog
module \Estágio_EX  (
  input  [31:0] RD1,
  input  [31:0] RD2,
  input  [31:0] Imm,
  input  [2:0] funct3,
  input  funct7_5,
  input  [1:0] Aluop,
  input  AluSrc,
  input  reset,
  input  clk,
  input  [31:0] PC_out,
  output [31:0] Result,
  output Zero,
  output [31:0] Branch_target_in
);

  wire [3:0] alu_control_1_y;
  wire [31:0] barrelshifter_1_out, multiplexer_1_out;

  Multiplexer #(.Bits(32)) multiplexer_1 (.sel(AluSrc), .in_0(RD2), .in_1(Imm), .out(multiplexer_1_out));
  Alu_control alu_control_1 (.AluOP(Aluop), .funct_3(funct3), .funct7_5(funct7_5), .Y(alu_control_1_y));
  BarrelShifter #(.Bits(32)) barrelshifter_1 (.in(Imm), .shift(6'b000001), .out(barrelshifter_1_out));
  alu_vhdl alu_vhdl_1 (
    .clk(clk), .reset(reset), .a(RD1), .b(multiplexer_1_out), .c(alu_control_1_y), .out(Result),
    .zero_flag(Zero));
  // adder adder_1: pin names not known; wires that end beside it: barrelshifter_1_out, PC_out, Branch_target_in
endmodule
