// Digital circuit Iparser2.dig as structural Verilog
module Iparser2 (
  input  [31:0] in_1,
  output [6:0] out_2,
  output [4:0] out_3,
  output [4:0] out_4,
  output [4:0] out_5,
  output [2:0] out_6,
  output [6:0] out_7,
  output [31:0] out_8,
  output [2:0] out_9
);

  Instruction_parser_2 #(.applicationType("GHDL")) u_Instruction_parser_2 (
    .instruction_in(in_1), .opcode_out(out_2), .rd_out(out_3), .rs1_out(out_4), .rs2_out(out_5),
    .funct3_out(out_6), .funct7_out(out_7), .imm_out(out_8), .inst_type_out(out_9));
endmodule

/* Code of Instruction_parser_2:
library ieee;
use ieee.std_logic_1164.all;
use ieee.numeric_std.all;

entity Instruction_parser_2 is
	port (
		instruction_in : in std_logic_vector(31 downto 0);
		opcode_out      : out std_logic_vector(6 downto 0);  -- bits 6-0
		rd_out          : out std_logic_vector(4 downto 0);
        	rs1_out         : out std_logic_vector(4 downto 0);
        	rs2_out         : out std_logic_vector(4 downto 0);
		funct3_out	: out std_logic_vector(2 downto 0);
		funct7_out	: out std_logic_vector(6 downto 0);
		imm_out		: out std_logic_vector(31 downto 0);
		inst_type_out   : out std_logic_vector(2 downto 0)
	);
end entity Instruction_parser_2;


architecture behavioral of Instruction_parser_2 is
begin
  process(instruction_in)
  begin
    opcode_out <= instruction_in(6  downto 0);
    rd_out     <= instruction_in(11 downto 7);
    rs1_out    <= instruction_in(19 downto 15);
    rs2_out    <= instruction_in(24 downto 20);
    funct3_out <= instruction_in(14 downto 12);
    funct7_out <= instruction_in(31 downto 25);

    case opcode_out is
      when "0110011" =>  -- R‑type
        inst_type_out <= "000";
        imm_out       <= (others => '0');

      when "0010111" =>  -- U‑type (AUIPC)
        inst_type_out <= "001";
        imm_out       <= std_logic_vector(to_unsigned(0,12)) & instruction_in(31 downto 12);

      when "0010011" | "0000011" | "1100111" =>  -- I‑type
        inst_type_out <= "010";
        imm_out       <= std_logic_vector(to_unsigned(0,20)) & instruction_in(31 downto 20);

      when "0100011" =>  -- S‑type (STORE)
        inst_type_out <= "011";
        imm_out       <= std_logic_vector(to_unsigned(0,20))
                         & instruction_in(31 downto 25)
                         & instruction_in(11 downto 7);

      when "1100011" =>  -- B‑type (BRANCH)
        inst_type_out <= "101";
        imm_out       <= std_logic_vector(to_unsigned(0,20))
                         & instruction_in(31)
                         & instruction_in(7)
                         & instruction_in(30 downto 25)
                         & instruction_in(11 downto 8)
                         & '0';

      when "1101111" =>  -- J‑type (JAL)
        inst_type_out <= "100";
        imm_out       <= std_logic_vector(to_unsigned(0,12))
                         & instruction_in(31)
                         & instruction_in(19 downto 12)
                         & instruction_in(20)
                         & instruction_in(30 downto 21)
                         & '0';

      when others =>
        inst_type_out <= "XXX";
        imm_out       <= (others => '0');
    end case;
  end process;
end architecture behavioral;
*/
