// Digital circuit blocoWB.dig as structural Verilog
module blocoWB (
  input  [31:0] ALUresult_in,
  input  [31:0] ReadData_in,
  input  memToReg_in,
  output [31:0] WriteData_out
);

  Multiplexer #(.Bits(32)) multiplexer_1 (
    .sel(memToReg_in), .in_0(ALUresult_in), .in_1(ReadData_in), .out(WriteData_out));
endmodule
