// Digital circuit ID_test.dig as structural Verilog
module ID_test (
  input  clk,
  input  in_13,
  output [31:0] out_1,
  output [31:0] _32,
  output [31:0] out_3,
  output [1:0] _2,
  output out_5,
  output out_6,
  output out_7,
  output out_8,
  output out_9,
  output out_10,
  output out_11,
  output [6:0] out_14,
  output [4:0] out_15
);

  wire button_1_out;
  wire [4:0] u_instruction_parser_rs1_o, u_instruction_parser_rs2_o;

  instruction_parser #(.applicationType("GHDL")) u_instruction_parser (
    .instruction_i(32'hfe211ae3), .opcode_o(out_14), .rd_o(out_15), .rs1_o(u_instruction_parser_rs1_o),
    .rs2_o(u_instruction_parser_rs2_o));
  Button button_1 (.out(button_1_out));
  control_unit #(.applicationType("GHDL")) u_control_unit (
    .reset(button_1_out), .opcode(out_14), .reg_write(out_11), .mem_to_reg(out_10), .mem_read(out_9),
    .mem_write(out_8), .alu_src(out_7), .branch(out_6), .jump(out_5), .alu_op(_2));
  register_file #(.applicationType("GHDL")) u_register_file (
    .clk(clk), .reg_write(in_13), .rs1_addr(u_instruction_parser_rs1_o),
    .rs2_addr(u_instruction_parser_rs2_o), .rd_addr(out_15), .rd_data(32'h1), .rs1_data(_32), .rs2_data(out_3));
  immediate_extractor #(.applicationType("GHDL")) u_immediate_extractor (
    .instruction_i(32'hfe211ae3), .immediate_o(out_1));
endmodule

/* Code of instruction_parser:
library ieee;
use ieee.std_logic_1164.all;

entity instruction_parser is
    port (
        instruction_i : in  std_logic_vector(31 downto 0); -- 32-bit RISC-V instruction

        -- Extracted fields
        opcode_o      : out std_logic_vector(6 downto 0);  -- bits 6-0
        rd_o          : out std_logic_vector(4 downto 0);  -- bits 11-7
        rs1_o         : out std_logic_vector(4 downto 0);  -- bits 19-15
        rs2_o         : out std_logic_vector(4 downto 0)  -- bits 24-20
    );
end entity instruction_parser;

architecture behavioral of instruction_parser is
begin

    -- Simple direct assignments for common fields
    opcode_o <= instruction_i(6 downto 0);
    rd_o     <= instruction_i(11 downto 7);
    rs1_o    <= instruction_i(19 downto 15);
    rs2_o    <= instruction_i(24 downto 20);

end architecture behavioral;
*/

/* Code of control_unit:
library ieee;
use ieee.std_logic_1164.all;

entity control_unit is
    port (
        -- Inputs
        reset       : in  std_logic;              -- Asynchronous reset signal
        opcode      : in  std_logic_vector(6 downto 0); -- 7-bit opcode from the instruction

        -- Outputs: Control signals for the datapath
        reg_write   : out std_logic;              -- Enable writing to the register file
        mem_to_reg  : out std_logic;              -- Selects if data from memory goes to the register file (for loads)
        mem_read    : out std_logic;              -- Enables reading from data memory
        mem_write   : out std_logic;              -- Enables writing to data memory
        alu_src     : out std_logic;              -- Selects the second ALU source:
                                                  -- '0' = rs2 data (for R-type)
                                                  -- '1' = immediate (for I, S, B, U, J-types)
        branch      : out std_logic;              -- Indicates a conditional branch instruction
        jump        : out std_logic;              -- Indicates an unconditional jump instruction (JAL, JALR)
        alu_op      : out std_logic_vector(1 downto 0) -- Controls the ALU's main operation:
                                                  -- "00" = Add (for Loads/Stores/AUIPC/LUI/JAL/JALR address calc or pass-through)
                                                  -- "01" = Subtract (for Branches for comparison)
                                                  -- "10" = R-type operation (further decoded by funct3/funct7)
                                                  -- "11" = I-type operation (further decoded by funct3)
    );
end entity control_unit;

architecture behavioral of control_unit is
    -- Define the opcodes for different instruction types as constants for readability
    constant R_TYPE_OP   : std_logic_vector(6 downto 0) := "0110011"; -- OP (e.g., ADD, SUB, AND, OR, XOR)
    constant I_TYPE_OP   : std_logic_vector(6 downto 0) := "0010011"; -- OP-IMM (e.g., ADDI, ANDI, ORI)
    constant L_TYPE_OP   : std_logic_vector(6 downto 0) := "0000011"; -- LOAD (e.g., LW)
    constant S_TYPE_OP   : std_logic_vector(6 downto 0) := "0100011"; -- STORE (e.g., SW)
    constant B_TYPE_OP   : std_logic_vector(6 downto 0) := "1100011"; -- BRANCH (e.g., BEQ, BNE)
    constant JAL_OP      : std_logic_vector(6 downto 0) := "1101111"; -- JAL (Jump and Link)
    constant JALR_OP     : std_logic_vector(6 downto 0) := "1100111"; -- JALR (Jump and Link Register)
    constant LUI_OP      : std_logic_vector(6 downto 0) := "0110111"; -- LUI (Load Upper Immediate)
    constant AUIPC_OP    : std_logic_vector(6 downto 0) := "0010111"; -- AUIPC (Add Upper Immediate to PC)

begin

    -- Main control logic process.
    -- This process is sensitive to both 'reset' and 'opcode'.
    -- All output signals must be assigned within this single process to avoid latches.
    process(reset, opcode)
    begin
        -- Handle asynchronous reset with highest priority.
        -- When 'reset' is '1', all control signals are forced to their inactive state.
        if reset = '1' then
            reg_write  <= '0';
            mem_to_reg <= '0';
            mem_read   <= '0';
            mem_write  <= '0';
            alu_src    <= '0';
            branch     <= '0';
            jump       <= '0';
            alu_op     <= "00"; -- Default ALU operation (e.g., add or pass-through)
        else
            -- Default assignments for all control signals when not under reset.
            -- This ensures that for any opcode not explicitly covered in the case
            -- statement (or before an opcode is processed), signals have a known,
            -- safe default (e.g., NOP-like behavior, no writes, no branches/jumps).
            reg_write  <= '0';
            mem_to_reg <= '0';
            mem_read   <= '0';
            mem_write  <= '0';
            alu_src    <= '0';
            branch     <= '0';
            jump       <= '0';
            alu_op     <= "00"; -- Default to "00" (Add/Pass-through) for ALU

            -- Use a case statement to decode the opcode and assert specific control signals.
            case opcode is
                -- R-Type instructions (e.g., ADD, SUB, AND, OR)
                -- Perform register-to-register operations, write result back to register file.
                when R_TYPE_OP =>
                    reg_write  <= '1';     -- Enable write to register file
                    alu_src    <= '0';     -- Second ALU operand comes from rs2 (register value)
                    alu_op     <= "10";    -- ALU performs R-type specific operation (decoded by ALU Control)

                -- I-Type instructions (Arithmetic/Logical with Immediate, excluding Loads/JALR)
                -- (e.g., ADDI, ANDI, ORI)
                -- Perform operation with immediate, write result back to register file.
                when I_TYPE_OP =>
                    reg_write  <= '1';     -- Enable write to register file
                    alu_src    <= '1';     -- Second ALU operand comes from immediate
                    alu_op     <= "11";    -- ALU performs I-type specific operation (decoded by ALU Control)

                -- Load instructions (I-type, e.g., LW)
                -- Calculate memory address using immediate, read from memory, write to register file.
                when L_TYPE_OP =>
                    reg_write  <= '1';     -- Enable write to register file
                    mem_to_reg <= '1';     -- Data from memory is written to reg file
                    mem_read   <= '1';     -- Enable memory read
                    alu_src    <= '1';     -- Second ALU operand is immediate (for address calculation)
                    alu_op     <= "00";    -- ALU performs addition (base register + immediate offset)

                -- Store instructions (S-type, e.g., SW)
                -- Calculate memory address using immediate, write to memory.
                when S_TYPE_OP =>
                    mem_write  <= '1';     -- Enable memory write
                    alu_src    <= '1';     -- Second ALU operand is immediate (for address calculation)
                    alu_op     <= "00";    -- ALU performs addition (base register + immediate offset)

                -- Branch instructions (B-type, e.g., BEQ, BNE)
                -- Compare two registers, enable branch if condition met.
                when B_TYPE_OP =>
                    branch     <= '1';     -- Indicate a branch instruction
                    alu_op     <= "01";    -- ALU performs subtraction (for comparison)

                -- LUI (Load Upper Immediate)
                -- Loads a 20-bit immediate into the upper 20 bits of a register, clearing lower 12.
                when LUI_OP =>
                    reg_write  <= '1';     -- Enable write to register file
                    alu_src    <= '1';     -- Immediate is used by ALU (often conceptually for a pass-through or add 0)
                    alu_op     <= "00";    -- ALU performs addition (effectively passes the immediate)

                -- AUIPC (Add Upper Immediate to PC)
                -- Adds a 20-bit immediate (shifted) to the PC, writes to register.
                when AUIPC_OP =>
                    reg_write  <= '1';     -- Enable write to register file
                    alu_src    <= '1';     -- Immediate is used by ALU
                    alu_op     <= "00";    -- ALU performs addition (PC + immediate)

                -- JAL (Jump and Link)
                -- Unconditional jump, saves PC+4 to rd.
                when JAL_OP =>
                    reg_write  <= '1';     -- Enable write to register file (for PC+4)
                    jump       <= '1';     -- Indicate an unconditional jump
                    alu_op     <= "00";    -- ALU may be used to calculate target address (PC + immediate) or pass PC+4

                -- JALR (Jump and Link Register)
                -- Unconditional jump to (rs1 + immediate), saves PC+4 to rd.
                when JALR_OP =>
                    reg_write  <= '1';     -- Enable write to register file (for PC+4)
                    jump       <= '1';     -- Indicate an unconditional jump
                    alu_src    <= '1';     -- Immediate is used by ALU (for address calculation)
                    alu_op     <= "00";    -- ALU performs addition (rs1 + immediate)

                -- Default case for any other undefined or unsupported opcodes.
                -- All control signals remain in their default inactive state.
                when others =>
                    null; -- Explicitly do nothing, as defaults are set above.
            end case;
        end if;
    end process;

end architecture behavioral;
*/

/* Code of register_file:
library ieee;
use ieee.std_logic_1164.all;
use ieee.numeric_std.all;

entity register_file is
    port (
        clk      : in  std_logic;
        reg_write: in  std_logic; -- Control signal to enable writing
        rs1_addr : in  std_logic_vector(4 downto 0);
        rs2_addr : in  std_logic_vector(4 downto 0);
        rd_addr  : in  std_logic_vector(4 downto 0);
        rd_data  : in  std_logic_vector(31 downto 0);
        rs1_data : out std_logic_vector(31 downto 0);
        rs2_data : out std_logic_vector(31 downto 0)
    );
end entity register_file;

architecture behavioral of register_file is
    -- Define the storage for 32 registers, each 32 bits wide
    type reg_array is array (0 to 31) of std_logic_vector(31 downto 0);
    signal registers : reg_array := (others => (others => '0'));

begin

    -- Read Process: Synchronous to the rising edge (first half of the clock)
    read_proc: process(clk)
    begin
        if rising_edge(clk) then
            -- Read rs1. Reading x0 always returns zero.
            if rs1_addr = "00000" then
                rs1_data <= (others => '0');
            else
                rs1_data <= registers(to_integer(unsigned(rs1_addr)));
            end if;

            -- Read rs2. Reading x0 always returns zero.
            if rs2_addr = "00000" then
                rs2_data <= (others => '0');
            else
                rs2_data <= registers(to_integer(unsigned(rs2_addr)));
            end if;
        end if;
    end process read_proc;

    -- Write Process: Synchronous to the falling edge (second half of the clock)
    write_proc: process(clk)
    begin
        if falling_edge(clk) then
            -- Write only if reg_write is enabled and the destination is not x0
            if reg_write = '1' and rd_addr /= "00000" then
                registers(to_integer(unsigned(rd_addr))) <= rd_data;
            end if;
        end if;
    end process write_proc;

end architecture behavioral;
*/

/* Code of immediate_extractor:
library ieee;
use ieee.std_logic_1164.all;
use ieee.numeric_std.all;

entity immediate_extractor is
    port (
        instruction_i : in  std_logic_vector(31 downto 0);
        immediate_o   : out std_logic_vector(31 downto 0)
    );
end entity immediate_extractor;

architecture behavioral of immediate_extractor is
    signal opcode_s : std_logic_vector(6 downto 0);
begin

    opcode_s <= instruction_i(6 downto 0);

    process(instruction_i, opcode_s)
        variable imm : std_logic_vector(31 downto 0);
    begin
        case opcode_s is
            -- I-type
            when "0000011" | "0010011" | "1100111" =>
                imm := (others => instruction_i(31));
                imm(11 downto 0) := instruction_i(31 downto 20);
                immediate_o <= imm;

            -- S-type
            when "0100011" =>
                imm := (others => instruction_i(31));
                imm(11 downto 5) := instruction_i(31 downto 25);
                imm(4 downto 0)  := instruction_i(11 downto 7);
                immediate_o <= imm;

            -- B-type
            when "1100011" =>
                imm := (others => instruction_i(31));
                imm(12)         := instruction_i(31);
                imm(11)         := instruction_i(7);
                imm(10 downto 5):= instruction_i(30 downto 25);
                imm(4 downto 1) := instruction_i(11 downto 8);
                imm(0)          := '0';
                immediate_o <= imm;

            -- U-type
            when "0110111" | "0010111" =>
                imm := instruction_i(31 downto 12) & (11 downto 0 => '0');
                immediate_o <= imm;

            -- J-type
            when "1101111" =>
                imm := (others => instruction_i(31));
                imm(20)         := instruction_i(31);
                imm(19 downto 12):= instruction_i(19 downto 12);
                imm(11)         := instruction_i(20);
                imm(10 downto 1):= instruction_i(30 downto 21);
                imm(0)          := '0';
                immediate_o <= imm;

            -- Default
            when others =>
                immediate_o <= (others => '0');
        end case;
    end process;

end architecture behavioral;
*/
