// Digital circuit CPU6.dig as structural Verilog
module CPU6 (
  input  clk,
  output [6:0] out_1,
  output [4:0] out_2,
  output [4:0] out_3,
  output [4:0] out_4,
  output [31:0] out_5,
  output [1:0] out_6,
  output out_7,
  output out_8,
  output out_9,
  output out_10,
  output out_11,
  output out_12,
  output out_13,
  output out_14,
  output out_15,
  output out_16,
  output [31:0] out_17,
  output [31:0] out_18,
  output [31:0] out_19,
  output [4:0] out_20,
  output [31:0] out_21,
  output [23:0] out_22,
  output out_23,
  output [31:0] pc_o,
  output [31:0] Instruction_Out,
  output [31:0] out_27,
  output [31:0] pc,
  output out_29,
  output [31:0] out_30
);

  wire alu_vhdl_1_zero_flag, EXMEMbubble, IDEXbubble, IFIDbubble, IFIDfreeze, PCfreeze, RegWrite_EXMEM,
       RegWrite_IDEX, reset, u_EX_MEM_Pipeline_branch_out, u_EX_MEM_Pipeline_memread_out,
       u_EX_MEM_Pipeline_memtoreg_out, u_EX_MEM_Pipeline_memwrite_out, u_EX_MEM_Pipeline_zero_out,
       u_ID_EX_Pipeline_alusrc_out, u_ID_EX_Pipeline_branch_out, u_ID_EX_Pipeline_funct_7_5,
       u_ID_EX_Pipeline_jump_out, u_ID_EX_Pipeline_memread_out, u_ID_EX_Pipeline_memtoreg_out,
       u_ID_EX_Pipeline_memwrite_out;
  wire [1:0] u_ID_EX_Pipeline_aluop_out;
  wire [2:0] u_ID_EX_Pipeline_funct_3_out, u_instruction_parser_funct_3;
  wire [3:0] alu_control_1_y;
  wire [4:0] rd_EXMEM, rd_IDEX;
  wire [6:0] u_instruction_parser_funct_7;
  wire [23:0] novoblocoif_1_inst_addr;
  wire [31:0] adder_1_p3, alu_vhdl_1_out, barrelshifter_1_out, eepromdualport_1_d, multiplexer_1_out,
       novoblocoif_1_pc_out, u_EX_MEM_Pipeline_writedata_out, u_ID_EX_Pipeline_imm_out,
       u_ID_EX_Pipeline_pc_out, u_ID_EX_Pipeline_rs1_data_out, u_ID_EX_Pipeline_rs2_data_out,
       u_register_file_rs1_data, u_register_file_rs2_data;

  Button button_1 (.out(reset));
  novoblocoIF novoblocoif_1 (
    .jump(out_29), .jump_pc(out_30), .pc_in(pc), .inst_addr(novoblocoif_1_inst_addr),
    .pc_out(novoblocoif_1_pc_out));
  pc #(.applicationType("GHDL")) u_pc (
    .pc_i(novoblocoif_1_pc_out), .clk(clk), .reset(reset), .freeze(PCfreeze), .pc_o(pc));
  ROM #(.AddrBits(24), .Bits(32)) inst_memory (.A(novoblocoif_1_inst_addr), .sel(1'b1), .D(out_27));
  IFID #(.applicationType("GHDL")) u_IFID (
    .pc_i(pc), .inst_i(out_27), .clk(clk), .reset(reset), .freeze(IFIDfreeze), .bubble(IFIDbubble),
    .pc_o(pc_o), .inst_o(Instruction_Out));
  HDU #(.applicationType("GHDL")) u_HDU (
    .rs1(out_2), .rs2(out_3), .opcode(out_1), .rd_IDEX(rd_IDEX), .RegWrite_IDEX(RegWrite_IDEX),
    .rd_EXMEM(rd_EXMEM), .RegWrite_EXMEM(RegWrite_EXMEM), .rd_MEMWB(out_20), .RegWrite_MEMWB(out_15),
    .jump(out_29), .PC_freeze(PCfreeze), .IFID_freeze(IFIDfreeze), .IFID_bubble(IFIDbubble),
    .IDEX_bubble(IDEXbubble), .EXMEM_bubble(EXMEMbubble));
  instruction_parser #(.applicationType("GHDL")) u_instruction_parser (
    .instruction_i(Instruction_Out), .opcode_o(out_1), .rd_o(out_4), .funct_3(u_instruction_parser_funct_3),
    .rs1_o(out_2), .rs2_o(out_3), .funct_7(u_instruction_parser_funct_7));
  register_file #(.applicationType("GHDL")) u_register_file (
    .clk(clk), .reset(reset), .reg_write(out_15), .rs1_addr(out_2), .rs2_addr(out_3), .rd_addr(out_4),
    .rd_data(out_19), .rs1_data(u_register_file_rs1_data), .rs2_data(u_register_file_rs2_data));
  immediate_extractor #(.applicationType("GHDL")) u_immediate_extractor (
    .instruction_i(Instruction_Out), .immediate_o(out_5));
  control_unit #(.applicationType("GHDL")) u_control_unit (
    .opcode(out_1), .alu_op(out_6), .alu_src(out_7), .mem_read(out_8), .mem_write(out_9),
    .mem_to_reg(out_10), .reg_write(out_11), .branch(out_12), .jump(out_13));
  ID_EX_Pipeline #(.applicationType("GHDL")) u_ID_EX_Pipeline (
    .clk(clk), .reset(reset), .ALUOp_in(out_6), .ALUSrc_in(out_7), .memRead_in(out_8), .memWrite_in(out_9),
    .memToReg_in(out_10), .regWrite_in(out_11), .branch_in(out_12), .jump_in(out_13),
    .Rs1_data_in(u_register_file_rs1_data), .Rs2_data_in(u_register_file_rs2_data), .Imm_in(out_5),
    .Rs1_in(out_2), .Rs2_in(out_3), .Rd_in(out_4), .PC_in(pc_o), .funct_3_in(u_instruction_parser_funct_3),
    .funct_7_in(u_instruction_parser_funct_7), .bubble(IDEXbubble), .ALUOp_out(u_ID_EX_Pipeline_aluop_out),
    .ALUSrc_out(u_ID_EX_Pipeline_alusrc_out), .memRead_out(u_ID_EX_Pipeline_memread_out),
    .memWrite_out(u_ID_EX_Pipeline_memwrite_out), .memToReg_out(u_ID_EX_Pipeline_memtoreg_out),
    .regWrite_out(RegWrite_IDEX), .branch_out(u_ID_EX_Pipeline_branch_out),
    .jump_out(u_ID_EX_Pipeline_jump_out), .Rs1_data_out(u_ID_EX_Pipeline_rs1_data_out),
    .Rs2_data_out(u_ID_EX_Pipeline_rs2_data_out), .Imm_out(u_ID_EX_Pipeline_imm_out), .Rd_out(rd_IDEX),
    .PC_out(u_ID_EX_Pipeline_pc_out), .funct_3_out(u_ID_EX_Pipeline_funct_3_out),
    .funct_7_5(u_ID_EX_Pipeline_funct_7_5));  // open: Rs1_out, Rs2_out
  Alu_control alu_control_1 (
    .AluOP(u_ID_EX_Pipeline_aluop_out), .funct_3(u_ID_EX_Pipeline_funct_3_out),
    .funct7_5(u_ID_EX_Pipeline_funct_7_5), .Y(alu_control_1_y));
  Multiplexer #(.Bits(32)) multiplexer_1 (
    .sel(u_ID_EX_Pipeline_alusrc_out), .in_0(u_ID_EX_Pipeline_rs2_data_out), .in_1(u_ID_EX_Pipeline_imm_out),
    .out(multiplexer_1_out));
  alu_vhdl alu_vhdl_1 (
    .clk(clk), .reset(reset), .a(u_ID_EX_Pipeline_rs1_data_out), .b(multiplexer_1_out), .c(alu_control_1_y),
    .out(alu_vhdl_1_out), .zero_flag(alu_vhdl_1_zero_flag));
  BarrelShifter #(.Bits(32)) barrelshifter_1 (
    .in(u_ID_EX_Pipeline_pc_out), .shift(6'b000001), .out(barrelshifter_1_out));
  // adder adder_1: pin names not known; wires that end beside it: u_ID_EX_Pipeline_imm_out, barrelshifter_1_out, adder_1_p3
  EX_MEM_Pipeline #(.applicationType("GHDL")) u_EX_MEM_Pipeline (
    .clk(clk), .reset(reset), .MemRead_in(u_ID_EX_Pipeline_memread_out),
    .MemWrite_in(u_ID_EX_Pipeline_memwrite_out), .MemToReg_in(u_ID_EX_Pipeline_memtoreg_out),
    .RegWrite_in(RegWrite_IDEX), .branch_in(u_ID_EX_Pipeline_branch_out),
    .jump_in(u_ID_EX_Pipeline_jump_out), .ALUResult_in(alu_vhdl_1_out),
    .WriteData_in(u_ID_EX_Pipeline_rs2_data_out), .Rd_in(rd_IDEX), .zero_in(alu_vhdl_1_zero_flag),
    .branch_target_in(adder_1_p3), .bubble(EXMEMbubble), .MemRead_out(u_EX_MEM_Pipeline_memread_out),
    .MemWrite_out(u_EX_MEM_Pipeline_memwrite_out), .MemToReg_out(u_EX_MEM_Pipeline_memtoreg_out),
    .RegWrite_out(RegWrite_EXMEM), .ALUResult_out(out_21), .WriteData_out(u_EX_MEM_Pipeline_writedata_out),
    .Rd_out(rd_EXMEM), .branch_out(u_EX_MEM_Pipeline_branch_out), .jump_out(out_23),
    .zero_out(u_EX_MEM_Pipeline_zero_out), .branch_target_out(out_30));
  and and_1 (out_14, u_EX_MEM_Pipeline_branch_out, u_EX_MEM_Pipeline_zero_out);
  addr_trunc32to24 #(.applicationType("GHDL")) u_addr_trunc32to24 (.addr_32(out_21), .addr_24(out_22));
  or or_1 (out_29, out_14, out_23);
  EEPROMDualPort #(.AddrBits(24), .Bits(32)) eepromdualport_1 (
    .A(out_22), .Din(u_EX_MEM_Pipeline_writedata_out), .str(u_EX_MEM_Pipeline_memwrite_out), .C(clk),
    .ld(u_EX_MEM_Pipeline_memread_out), .D(eepromdualport_1_d));
  MEM_WB_Pipeline #(.applicationType("GHDL")) u_MEM_WB_Pipeline (
    .clk(clk), .reset(reset), .MemToReg_in(u_EX_MEM_Pipeline_memtoreg_out), .RegWrite_in(RegWrite_EXMEM),
    .ReadData_in(eepromdualport_1_d), .ALUResult_in(out_21), .Rd_in(rd_EXMEM), .MemToReg_out(out_16),
    .RegWrite_out(out_15), .ALUResult_out(out_17), .ReadData_out(out_18), .Rd_out(out_20));
  Multiplexer #(.Bits(32)) multiplexer_2 (.sel(out_16), .in_0(out_17), .in_1(out_18), .out(out_19));

  // Other names for the same wires on the sheet: branch_target[31:0] = out_30; hdu_opcode[6:0] = out_1;
  //   hdu_rs1[4:0] = out_2; hdu_rs2[4:0] = out_3; jump = out_29; rd_MEMWB[4:0] = out_20; RegWrite_MEMWB = out_15

  // Notes on the sheet:
  //   pc_o: Saída PC do registrador IF/ID
  //   Instruction_Out: Saída instruction do registrador IF/ID
  //   pc: Valor atual de PC
  //   Estágio IF
  //   contents of inst_memory (hex, n*v repeats v):
  //   108093,108093,6*0,2000ef
endmodule

/* Code of pc:
-- Registrador de 32 bits com entradas PCin, clk, reset e saída PCout

library IEEE;
use IEEE.STD_LOGIC_1164.ALL;

entity pc is
	Port (
    	pc_i : in std_logic_vector(31 downto 0);
    	clk: in std_logic;
        reset: in std_logic;

		freeze: in std_logic;

        pc_o: out std_logic_vector(31 downto 0)
    	);
end pc;

architecture Behavioral of pc is

begin

process(clk, reset)
begin
	if reset = '1' then
		pc_o <= X"00000000";

	elsif rising_edge(clk) and freeze = '0' then

		pc_o <= pc_i;

	end if;
end process;

end Behavioral;
*/

/* Code of IFID:
-- Registrador que guarda os dados necessários entre IF e ID. Esses dados são o valor de PC e a instrução da vez
library IEEE;
use IEEE.STD_LOGIC_1164.ALL;

entity IFID is
	Port (
    	pc_i : in std_logic_vector(31 downto 0);
        inst_i: in std_logic_vector(31 downto 0);

    	clk: in std_logic;
        reset: in std_logic;

		freeze: in std_logic;
		bubble: in std_logic;

        pc_o: out std_logic_vector(31 downto 0);
        inst_o: out std_logic_vector(31 downto 0)
    	);
end IFID;

architecture Behavioral of IFID is

begin

process(clk, reset)
begin
	if reset = '1' then
        pc_o <= X"00000000";
        inst_o <= X"00000000";

	elsif rising_edge(clk) then

		if freeze = '0' then
			if bubble = '1' then
				pc_o <= X"00000000";
				inst_o <= X"00000000";
			else
				pc_o <= pc_i;
				inst_o <= inst_i;
			end if;
		end if;

	end if;
end process;

end Behavioral;
*/

/* Code of HDU:
library IEEE;
use IEEE.STD_LOGIC_1164.ALL;

entity HDU is
	Port (
        -- Entradas que vêm do estágio ID
        rs1: in std_logic_vector(4 downto 0);
        rs2: in std_logic_vector(4 downto 0);
        opcode: in std_logic_vector(6 downto 0);

        -- Entradas que vêm dos demais estágios
        rd_IDEX: in std_logic_vector(4 downto 0);
        RegWrite_IDEX: in std_logic;

        rd_EXMEM: in std_logic_vector(4 downto 0);
        RegWrite_EXMEM: in std_logic;

        rd_MEMWB: in std_logic_vector(4 downto 0);
        RegWrite_MEMWB: in std_logic;

        jump: in std_logic; -- Indica se será feito um salto este ciclo

    	-- Saídas
        -- Saídas freeze
        -- Se uma delas é '1', o registrador em questão mantém seu valor atual no próximo ciclo
        PC_freeze: out std_logic;
        IFID_freeze: out std_logic;

        -- Saídas bubble
        -- Se uma delas é '1', o registrador em questão recebe um NOP no próximo ciclo. Seu valor atual pode continuar se propagando ao longo da pipeline (pois o NOP é inserido de forma síncrona)
        IFID_bubble: out std_logic;
        IDEX_bubble: out std_logic;
        EXMEM_bubble: out std_logic
    	);
end HDU;

architecture Behavioral of HDU is

    -- Opcodes para diferentes tipos de instrução
    constant R_TYPE_OP   : std_logic_vector(6 downto 0) := "0110011"; -- OP (ADD, SUB, AND, OR, XOR)
    constant I_TYPE_OP   : std_logic_vector(6 downto 0) := "0010011"; -- OP-IMM (ADDI, ANDI, ORI)
    constant L_TYPE_OP   : std_logic_vector(6 downto 0) := "0000011"; -- LOAD (LW)
    constant S_TYPE_OP   : std_logic_vector(6 downto 0) := "0100011"; -- STORE (SW)
    constant B_TYPE_OP   : std_logic_vector(6 downto 0) := "1100011"; -- BRANCH (BEQ, BNE)
    constant JAL_OP      : std_logic_vector(6 downto 0) := "1101111"; -- JAL
    constant JALR_OP     : std_logic_vector(6 downto 0) := "1100111"; -- JALR
    constant LUI_OP      : std_logic_vector(6 downto 0) := "0110111"; -- LUI
    constant AUIPC_OP    : std_logic_vector(6 downto 0) := "0010111"; -- AUIPC

begin

process(rs1, rs2, opcode, rd_IDEX, RegWrite_IDEX, rd_EXMEM, RegWrite_EXMEM, rd_MEMWB, RegWrite_MEMWB, jump)

    variable inst_type: integer;

    -- inst_type = 1 indica que a instrução é jal, jalr, auipc, lui, ou seja, não está sujeita a hazard de escrita-leitura
    -- inst_type = 2 indica que a instrução é addi, andi, ori, xori, lli, srli, lw, sw, ou seja, está sujeita a hazard de escrita-leitura apenas em rs1
    -- inst_type = 3 indica que a instrução e add, sub, and, or, xor, sll, srl, beq, bne, ou seja, está sujeita a hazard de escrita-leitura em rs1 e rs2

    variable WriteReadHazard: std_logic; -- Indica que há um hazard de escrita-leitura

begin
    -- Primeiro, vamos verificar se há um jump acontecendo. Nesse caso, independentemente dos demais hazards, as instruções em IFID, IDEX estão erradas, e o valor de PC também está errado (está prestes a ser atualizado)
    -- Precisamos dar bubble em IFID, IDEX, EXMEM, e não congelar PC
    if jump = '1' then
        PC_freeze <= '0';
        IFID_freeze <= '0';

        IFID_bubble <= '1';
        IDEX_bubble <= '1';
        EXMEM_bubble <= '1';
    else

        -- Identificar se a instução em ID é tipo 1, 2, ou 3
        case opcode is
            when JAL_OP | JALR_OP | LUI_OP | AUIPC_OP =>
                inst_type := 1;
            when I_TYPE_OP | L_TYPE_OP | S_TYPE_OP =>
                inst_type := 2;
            when R_TYPE_OP | B_TYPE_OP =>
                inst_type := 3;
            when others =>
                -- No caso de instrução inválida, vou considerar como tipo 1 (não suscetível a hazard de escrita-leitura)
                inst_type := 1;
        end case;

        -- Identificar com base nisso se há hazard de escrita-leitura
        case inst_type is            
            when 2 =>
                if RegWrite_IDEX = '1' and rd_IDEX = rs1 then
                    writeReadHazard := '1';

                elsif RegWrite_EXMEM = '1' and rd_EXMEM = rs1 then
                    writeReadHazard := '1';
                
                elsif RegWrite_MEMWB = '1' and rd_MEMWB = rs1 then
                    writeReadHazard := '1';
                
                else
                    writeReadHazard := '0';
                
                end if;

            when 3 =>
                if RegWrite_IDEX = '1' and (rd_IDEX = rs1 or rd_IDEX = rs2) then
                    writeReadHazard := '1';

                elsif RegWrite_EXMEM = '1' and (rd_EXMEM = rs1 or rd_EXMEM = rs2) then
                    writeReadHazard := '1';

                elsif RegWrite_MEMWB = '1' and (rd_MEMWB = rs1 or rd_MEMWB = rs2) then
                    writeReadHazard := '1';

                else
                    writeReadHazard := '0';

                end if;

            when others =>
                -- No tipo 1, não temos hazard de escrita-leitura
                writeReadHazard := '0';
        end case;

        -- De acordo com writeReadHazard, decidimos as saídas
        if writeReadHazard = '1' then
            -- Nesse caso, o valor que estamos lendo em ID está errado. Precisamos inserir bolha em IDEX para esse valor não se propagar, e congelar PC e IFID
            PC_freeze <= '1';
            IFID_freeze <= '1';

            IFID_bubble <= '0';
            IDEX_bubble <= '1';
            EXMEM_bubble <= '0';
        else
            -- Sem hazard
            PC_freeze <= '0';
            IFID_freeze <= '0';

            IFID_bubble <= '0';
            IDEX_bubble <= '0';
            EXMEM_bubble <= '0';
        end if;

    end if;

end process;

end Behavioral;
*/

/* Code of instruction_parser:
library ieee;
use ieee.std_logic_1164.all;

entity instruction_parser is
    port (
        instruction_i : in  std_logic_vector(31 downto 0); -- 32-bit RISC-V instruction

        -- Extracted fields
        opcode_o      : out std_logic_vector(6 downto 0);  -- bits 6-0
        rd_o          : out std_logic_vector(4 downto 0);  -- bits 11-7
        funct_3       : out std_logic_vector(2 downto 0);  -- bits 14-12
        rs1_o         : out std_logic_vector(4 downto 0);  -- bits 19-15
        rs2_o         : out std_logic_vector(4 downto 0); -- bits 24-20
        funct_7       : out std_logic_vector(6 downto 0)
    );
end entity instruction_parser;

architecture behavioral of instruction_parser is
begin

    -- Simple direct assignments for common fields
    opcode_o <= instruction_i(6 downto 0);
    rd_o     <= instruction_i(11 downto 7);
    funct_3  <= instruction_i(14 downto 12);
    rs1_o    <= instruction_i(19 downto 15);
    rs2_o    <= instruction_i(24 downto 20);
    funct_7  <= instruction_i(31 downto 25);

end architecture behavioral;
*/

/* Code of register_file:
library ieee;
use ieee.std_logic_1164.all;
use ieee.numeric_std.all;

entity register_file is
    port (
        clk      : in  std_logic;
        reset    : in  std_logic;
        reg_write: in  std_logic; -- Control signal to enable writing
        rs1_addr : in  std_logic_vector(4 downto 0);
        rs2_addr : in  std_logic_vector(4 downto 0);
        rd_addr  : in  std_logic_vector(4 downto 0);
        rd_data  : in  std_logic_vector(31 downto 0);
        rs1_data : out std_logic_vector(31 downto 0);
        rs2_data : out std_logic_vector(31 downto 0)
    );
end entity register_file;

architecture behavioral of register_file is
    -- Define the storage for 32 registers, each 32 bits wide
    type reg_array is array (0 to 31) of std_logic_vector(31 downto 0);
    signal registers : reg_array := (others => (others => '0'));

begin

    -- Reset Process: Asynchronous reset to clear all registers
    reset_proc: process(reset)
    begin
        if reset = '1' then
            -- Clear all registers to zero on reset
            for i in 0 to 31 loop
                registers(i) <= (others => '0');
            end loop;
        end if;
    end process reset_proc;

    -- Read Process: Synchronous to the rising edge (first half of the clock)
    read_proc: process(clk)
    begin
        if rising_edge(clk) then
            -- Read rs1. Reading x0 always returns zero.
            if rs1_addr = "00000" then
                rs1_data <= (others => '0');
            else
                rs1_data <= registers(to_integer(unsigned(rs1_addr)));
            end if;

            -- Read rs2. Reading x0 always returns zero.
            if rs2_addr = "00000" then
                rs2_data <= (others => '0');
            else
                rs2_data <= registers(to_integer(unsigned(rs2_addr)));
            end if;
        end if;
    end process read_proc;

    -- Write Process: Synchronous to the falling edge (second half of the clock)
    write_proc: process(clk)
    begin
        if falling_edge(clk) then
            -- Write only if reg_write is enabled and the destination is not x0
            if reg_write = '1' and rd_addr /= "00000" then
                registers(to_integer(unsigned(rd_addr))) <= rd_data;
            end if;
        end if;
    end process write_proc;

end architecture behavioral;
*/

/* Code of immediate_extractor:
library ieee;
use ieee.std_logic_1164.all;
use ieee.numeric_std.all; -- For signed arithmetic and type conversions

entity immediate_extractor is
    port (
        instruction_i : in  std_logic_vector(31 downto 0); -- 32-bit RISC-V instruction input
        immediate_o   : out std_logic_vector(31 downto 0)  -- 32-bit sign-extended immediate output
    );
end entity immediate_extractor;

architecture behavioral of immediate_extractor is
    -- Internal signal to hold the opcode (bits 6 downto 0) for use in the process.
    signal opcode_s : std_logic_vector(6 downto 0);
begin

    -- Extract the opcode from the instruction. This assignment is concurrent.
    opcode_s <= instruction_i(6 downto 0);

    -- This process block implements the combinational logic for immediate extraction.
    -- The sensitivity list includes all signals that, when changed, should
    -- re-evaluate the logic inside the process.
    process(instruction_i, opcode_s)
        -- Declare a local variable to build the immediate value before assigning it
        -- to the output signal. Variables are evaluated immediately within the process.
        variable imm : std_logic_vector(31 downto 0);
    begin
        -- Use a case statement to select the immediate extraction logic
        -- based on the instruction's opcode.
        case opcode_s is
            -- I-type immediate (Load, Op-Imm, JALR)
            -- Opcode values: 0x03 (LOAD), 0x13 (OP-IMM), 0x67 (JALR)
            -- Format: imm[11:0] is instruction[31:20]
            when "0000011" | "0010011" | "1100111" =>
                -- Sign-extend the 12-bit immediate: replicate bit 31 of the instruction
                -- (which is imm[11]) across the higher bits (31 downto 12) of the 32-bit immediate.
                imm := (others => instruction_i(31));
                -- Place the 12-bit immediate into the lower 12 bits of 'imm'.
                imm(11 downto 0) := instruction_i(31 downto 20);
                -- Assign the constructed immediate to the output.
                immediate_o <= imm;

            -- S-type immediate (Store)
            -- Opcode value: 0x23 (STORE)
            -- Format: imm[11:5] from instruction[31:25], imm[4:0] from instruction[11:7]
            -- Reconstructed: imm[11:5] << 5 | imm[4:0]
            when "0100011" =>
                -- Sign-extend the 12-bit immediate: use bit 31 of the instruction
                -- (which is imm[11]) for sign extension.
                imm := (others => instruction_i(31));
                -- Place the high part of the immediate (imm[11:5]) into its position.
                imm(11 downto 5) := instruction_i(31 downto 25);
                -- Place the low part of the immediate (imm[4:0]) into its position.
                imm(4 downto 0)  := instruction_i(11 downto 7);
                -- Assign the constructed immediate to the output.
                immediate_o <= imm;

            -- B-type immediate (Branch)
            -- Opcode value: 0x63 (BRANCH)
            -- Format: imm[12|10:5|4:1|11]
            -- Bits: instruction[31] (imm[12]), instruction[30:25] (imm[10:5]),
            --       instruction[11:8] (imm[4:1]), instruction[7] (imm[11])
            -- Reconstructed: imm[12] << 12 | imm[11] << 11 | imm[10:5] << 5 | imm[4:1] << 1 (imm[0] is always '0')
            when "1100011" =>
                -- Sign-extend the 13-bit immediate: use bit 31 of the instruction
                -- (which is imm[12]) for sign extension.
                imm := (others => instruction_i(31));
                -- Place fragmented immediate bits into their correct positions.
                imm(12)        := instruction_i(31);         -- imm[12]
                imm(11)        := instruction_i(7);          -- imm[11]
                imm(10 downto 5) := instruction_i(30 downto 25); -- imm[10:5]
                imm(4 downto 1) := instruction_i(11 downto 8);  -- imm[4:1]
                imm(0)         := '0';                       -- imm[0] is always 0 for branches
                -- Assign the constructed immediate to the output.
                immediate_o <= imm;

            -- U-type immediate (LUI, AUIPC)
            -- Opcode values: 0x37 (LUI), 0x17 (AUIPC)
            -- Format: imm[31:12] is instruction[31:12]
            -- This immediate is already effectively shifted left by 12 bits.
            when "0110111" | "0010111" =>
                -- Concatenate the upper 20 bits of the instruction with 12 zeros.
                -- No explicit sign extension needed, as the value is simply the upper bits.
                imm := instruction_i(31 downto 12) & (11 downto 0 => '0');
                -- Assign the constructed immediate to the output.
                immediate_o <= imm;

            -- J-type immediate (JAL)
            -- Opcode value: 0x6F (JAL)
            -- Format: imm[20|10:1|11|19:12]
            -- Bits: instruction[31] (imm[20]), instruction[19:12] (imm[19:12]),
            --       instruction[20] (imm[11]), instruction[30:21] (imm[10:1])
            -- Reconstructed: imm[20] << 20 | imm[19:12] << 12 | imm[11] << 11 | imm[10:1] << 1 (imm[0] is always '0')
            when "1101111" =>
                -- Sign-extend the 21-bit immediate: use bit 31 of the instruction
                -- (which is imm[20]) for sign extension.
                imm := (others => instruction_i(31));
                -- Place fragmented immediate bits into their correct positions.
                imm(20)        := instruction_i(31);         -- imm[20]
                imm(19 downto 12) := instruction_i(19 downto 12); -- imm[19:12]
                imm(11)        := instruction_i(20);         -- imm[11]
                imm(10 downto 1) := instruction_i(30 downto 21); -- imm[10:1]
                imm(0)         := '0';                       -- imm[0] is always 0 for jumps
                -- Assign the constructed immediate to the output.
                immediate_o <= imm;

            -- Default case: For unrecognized opcodes, output all zeros.
            when others =>
                imm := (others => '0');
                immediate_o <= imm;
        end case;
    end process;

end architecture behavioral;
*/

/* Code of control_unit:
library ieee;
use ieee.std_logic_1164.all;

entity control_unit is
    port (
        -- Inputs
        opcode      : in  std_logic_vector(6 downto 0); -- 7-bit opcode from the instruction

        -- Outputs: Control signals for the datapath
        alu_op      : out std_logic_vector(1 downto 0); -- Controls the ALU's main operation:
                                                  -- "00" = Add (for Loads/Stores/AUIPC/LUI/JAL/JALR address calc or pass-through)
                                                  -- "01" = Subtract (for Branches for comparison)
                                                  -- "10" = R-type operation (further decoded by funct3/funct7)
                                                  -- "11" = I-type operation (further decoded by funct3)
        alu_src     : out std_logic;              -- Selects the second ALU source:
                                                  -- '0' = rs2 data (for R-type)
                                                  -- '1' = immediate (for I, S, B, U, J-types)
        mem_read    : out std_logic;              -- Enables reading from data memory
        mem_write   : out std_logic;              -- Enables writing to data memory
        mem_to_reg  : out std_logic;              -- Selects if data from memory goes to the register file (for loads)
        reg_write   : out std_logic;              -- Enable writing to the register file
        branch      : out std_logic;              -- Indicates a conditional branch instruction
        jump        : out std_logic              -- Indicates an unconditional jump instruction (JAL, JALR)

    );
end entity control_unit;

architecture behavioral of control_unit is
    -- Define the opcodes for different instruction types as constants for readability
    constant R_TYPE_OP   : std_logic_vector(6 downto 0) := "0110011"; -- OP (e.g., ADD, SUB, AND, OR, XOR)
    constant I_TYPE_OP   : std_logic_vector(6 downto 0) := "0010011"; -- OP-IMM (e.g., ADDI, ANDI, ORI)
    constant L_TYPE_OP   : std_logic_vector(6 downto 0) := "0000011"; -- LOAD (e.g., LW)
    constant S_TYPE_OP   : std_logic_vector(6 downto 0) := "0100011"; -- STORE (e.g., SW)
    constant B_TYPE_OP   : std_logic_vector(6 downto 0) := "1100011"; -- BRANCH (e.g., BEQ, BNE)
    constant JAL_OP      : std_logic_vector(6 downto 0) := "1101111"; -- JAL (Jump and Link)
    constant JALR_OP     : std_logic_vector(6 downto 0) := "1100111"; -- JALR (Jump and Link Register)
    constant LUI_OP      : std_logic_vector(6 downto 0) := "0110111"; -- LUI (Load Upper Immediate)
    constant AUIPC_OP    : std_logic_vector(6 downto 0) := "0010111"; -- AUIPC (Add Upper Immediate to PC)

begin

    -- Main control logic process.
    -- This process is sensitive to both 'reset' and 'opcode'.
    -- All output signals must be assigned within this single process to avoid latches.
    process(opcode)
    begin
        -- safe default (e.g., NOP-like behavior, no writes, no branches/jumps).
        reg_write  <= '0';
        mem_to_reg <= '0';
        mem_read   <= '0';
        mem_write  <= '0';
        alu_src    <= '0';
        branch     <= '0';
        jump       <= '0';
        alu_op     <= "00"; -- Default to "00" (Add/Pass-through) for ALU

        -- Use a case statement to decode the opcode and assert specific control signals.
        case opcode is
            -- R-Type instructions (e.g., ADD, SUB, AND, OR)
            -- Perform register-to-register operations, write result back to register file.
            when R_TYPE_OP =>
                reg_write  <= '1';     -- Enable write to register file
                alu_src    <= '0';     -- Second ALU operand comes from rs2 (register value)
                alu_op     <= "10";    -- ALU performs R-type specific operation (decoded by ALU Control)

            -- I-Type instructions (Arithmetic/Logical with Immediate, excluding Loads/JALR)
            -- (e.g., ADDI, ANDI, ORI)
            -- Perform operation with immediate, write result back to register file.
            when I_TYPE_OP =>
                reg_write  <= '1';     -- Enable write to register file
                alu_src    <= '1';     -- Second ALU operand comes from immediate
                alu_op     <= "11";    -- ALU performs I-type specific operation (decoded by ALU Control)

            -- Load instructions (I-type, e.g., LW)
            -- Calculate memory address using immediate, read from memory, write to register file.
            when L_TYPE_OP =>
                reg_write  <= '1';     -- Enable write to register file
                mem_to_reg <= '1';     -- Data from memory is written to reg file
                mem_read   <= '1';     -- Enable memory read
                alu_src    <= '1';     -- Second ALU operand is immediate (for address calculation)
                alu_op     <= "00";    -- ALU performs addition (base register + immediate offset)

            -- Store instructions (S-type, e.g., SW)
            -- Calculate memory address using immediate, write to memory.
            when S_TYPE_OP =>
                mem_write  <= '1';     -- Enable memory write
                alu_src    <= '1';     -- Second ALU operand is immediate (for address calculation)
                alu_op     <= "00";    -- ALU performs addition (base register + immediate offset)

            -- Branch instructions (B-type, e.g., BEQ, BNE)
            -- Compare two registers, enable branch if condition met.
            when B_TYPE_OP =>
                branch     <= '1';     -- Indicate a branch instruction
                alu_op     <= "01";    -- ALU performs subtraction (for comparison)

            -- LUI (Load Upper Immediate)
            -- Loads a 20-bit immediate into the upper 20 bits of a register, clearing lower 12.
            when LUI_OP =>
                reg_write  <= '1';     -- Enable write to register file
                alu_src    <= '1';     -- Immediate is used by ALU (often conceptually for a pass-through or add 0)
                alu_op     <= "00";    -- ALU performs addition (effectively passes the immediate)

            -- AUIPC (Add Upper Immediate to PC)
            -- Adds a 20-bit immediate (shifted) to the PC, writes to register.
            when AUIPC_OP =>
                reg_write  <= '1';     -- Enable write to register file
                alu_src    <= '1';     -- Immediate is used by ALU
                alu_op     <= "00";    -- ALU performs addition (PC + immediate)

            -- JAL (Jump and Link)
            -- Unconditional jump, saves PC+4 to rd.
            when JAL_OP =>
                reg_write  <= '1';     -- Enable write to register file (for PC+4)
                jump       <= '1';     -- Indicate an unconditional jump
                alu_op     <= "00";    -- ALU may be used to calculate target address (PC + immediate) or pass PC+4

            -- JALR (Jump and Link Register)
            -- Unconditional jump to (rs1 + immediate), saves PC+4 to rd.
            when JALR_OP =>
                reg_write  <= '1';     -- Enable write to register file (for PC+4)
                jump       <= '1';     -- Indicate an unconditional jump
                alu_src    <= '1';     -- Immediate is used by ALU (for address calculation)
                alu_op     <= "00";    -- ALU performs addition (rs1 + immediate)

            -- Default case for any other undefined or unsupported opcodes.
            -- All control signals remain in their default inactive state.
            when others =>
                null; -- Explicitly do nothing, as defaults are set above.
        end case;
    end process;

end architecture behavioral;
*/

/* Code of ID_EX_Pipeline:
library IEEE;
use IEEE.STD_LOGIC_1164.ALL;
use IEEE.NUMERIC_STD.ALL;

entity ID_EX_Pipeline is
    Port (
        clk           : in  std_logic;
        reset         : in  std_logic;

        -- Control signals
        ALUOp_in      : in  std_logic_vector(1 downto 0);
        ALUSrc_in     : in  std_logic;
        memRead_in   : in  std_logic;
        memWrite_in  : in  std_logic;
        memToReg_in  : in  std_logic;
        regWrite_in  : in  std_logic;
        branch_in    : in  std_logic;
        jump_in      : in  std_logic;
        -- Data signals
        Rs1_data_in  : in  std_logic_vector(31 downto 0);
        Rs2_data_in  : in  std_logic_vector(31 downto 0);
        Imm_in : in  std_logic_vector(31 downto 0);
        Rs1_in         : in  std_logic_vector(4 downto 0);
        Rs2_in         : in  std_logic_vector(4 downto 0);
        Rd_in         : in  std_logic_vector(4 downto 0);
        PC_in         : in std_logic_vector(31 downto 0);
        funct_3_in      : in  std_logic_vector(2 downto 0);
        funct_7_in      : in  std_logic_vector(6 downto 0); 
        
        bubble        : in std_logic; -- Input de bubble síncrono

        -- Control outputs
        ALUOp_out     : out std_logic_vector(1 downto 0);
        ALUSrc_out    : out std_logic;
        memRead_out   : out std_logic;
        memWrite_out  : out std_logic;
        memToReg_out  : out std_logic;
        regWrite_out  : out std_logic;
        branch_out    : out std_logic;
        jump_out      : out std_logic;
        -- Data outputs
        Rs1_data_out       : out std_logic_vector(31 downto 0);
        Rs2_data_out       : out std_logic_vector(31 downto 0);
        Imm_out       : out std_logic_vector(31 downto 0);
        Rs1_out       : out std_logic_vector(4 downto 0);
        Rs2_out       : out std_logic_vector(4 downto 0);
        Rd_out        : out std_logic_vector(4 downto 0);
        PC_out        : out std_logic_vector(31 downto 0);
        funct_3_out     : out  std_logic_vector(2 downto 0);
        funct_7_5     : out  std_logic
    );
end ID_EX_Pipeline;

architecture Behavioral of ID_EX_Pipeline is
begin
    process(clk, reset)
    begin
        if reset = '1' then
            -- On reset, clear all outputs
            ALUOp_out      <= (others => '0');
            ALUSrc_out     <= '0';
            memRead_out    <= '0';
            memWrite_out   <= '0';
            memToReg_out   <= '0';
            regWrite_out   <= '0';
            branch_out     <= '0';
            jump_out       <= '0';
            Rs1_data_out       <= (others => '0');
            Rs2_data_out       <= (others => '0');
            Imm_out       <= (others => '0');
            Rs1_out         <= (others => '0');
            Rs2_out         <= (others => '0');
            Rd_out         <= (others => '0');
            PC_out         <= (others => '0');
        elsif rising_edge(clk) then
            if bubble = '1' then
                ALUOp_out      <= (others => '0');
                ALUSrc_out     <= '0';
                memRead_out    <= '0';
                memWrite_out   <= '0';
                memToReg_out   <= '0';
                regWrite_out   <= '0';
                branch_out     <= '0';
                jump_out       <= '0';
                Rs1_data_out       <= (others => '0');
                Rs2_data_out       <= (others => '0');
                Imm_out       <= (others => '0');
                Rs1_out         <= (others => '0');
                Rs2_out         <= (others => '0');
                Rd_out         <= (others => '0');
                PC_out         <= (others => '0');
            else
                -- On clock edge, latch inputs to outputs
                ALUOp_out      <= ALUOp_in;
                ALUSrc_out     <= ALUSrc_in;
                memRead_out    <= memRead_in;
                memWrite_out   <= memWrite_in;
                memToReg_out   <= memToReg_in;
                regWrite_out   <= regWrite_in;
                branch_out     <= branch_in;
                jump_out       <= jump_in;
                Rs1_data_out       <= Rs1_data_in;
                Rs2_data_out       <= Rs2_data_in;
                Imm_out       <= Imm_in;
                Rs1_out         <= Rs1_in;
                Rs2_out         <= Rs2_in;
                Rd_out         <= Rd_in;
                PC_out <= PC_in;
                funct_3_out <= funct_3_in;
                funct_7_5 <= funct_7_in(5);
            end if;
        end if;
    end process;
end Behavioral;
*/

/* Code of EX_MEM_Pipeline:
library IEEE;
use IEEE.STD_LOGIC_1164.ALL;
use IEEE.NUMERIC_STD.ALL;

entity EX_MEM_Pipeline is
    Port (
        clk          : in  std_logic;
        reset        : in  std_logic;

        -- Control signals
        MemRead_in   : in  std_logic;
        MemWrite_in  : in  std_logic;
        MemToReg_in  : in  std_logic;
        RegWrite_in  : in  std_logic;
        branch_in    : in  std_logic;
        jump_in      : in  std_logic;
        -- Data signals
        ALUResult_in : in  std_logic_vector(31 downto 0);
        WriteData_in : in  std_logic_vector(31 downto 0);
        Rd_in       : in  std_logic_vector(4 downto 0);
        zero_in       : in  std_logic;
        branch_target_in : in  std_logic_vector(31 downto 0);

        bubble       : in std_logic; -- Entrada de bubble síncrona

        -- Outputs to MEM stage
        MemRead_out  : out std_logic;
        MemWrite_out : out std_logic;
        MemToReg_out : out std_logic;
        RegWrite_out : out std_logic;
        ALUResult_out: out std_logic_vector(31 downto 0);
        WriteData_out: out std_logic_vector(31 downto 0);
        Rd_out       : out std_logic_vector(4 downto 0);
        branch_out   : out std_logic;
        jump_out     : out std_logic;
        zero_out     : out std_logic;
        branch_target_out : out std_logic_vector(31 downto 0)
    );
end EX_MEM_Pipeline;

architecture Behavioral of EX_MEM_Pipeline is
begin
    process(clk, reset)
    begin
        if reset = '1' then
            MemRead_out   <= '0';
            MemWrite_out  <= '0';
            RegWrite_out  <= '0';
            MemToReg_out  <= '0';
            ALUResult_out <= (others => '0');
            WriteData_out <= (others => '0');
            Rd_out   <= (others => '0');
            jump_out      <= '0';
            branch_out    <= '0';
            zero_out      <= '0';
            branch_target_out <= (others => '0');
        elsif rising_edge(clk) then
            if bubble = '1' then

                MemRead_out   <= '0';
                MemWrite_out  <= '0';
                RegWrite_out  <= '0';
                MemToReg_out  <= '0';
                ALUResult_out <= (others => '0');
                WriteData_out <= (others => '0');
                Rd_out   <= (others => '0');
                jump_out      <= '0';
                branch_out    <= '0';
                zero_out      <= '0';
                branch_target_out <= (others => '0');

            else
                MemRead_out   <= MemRead_in;
                MemWrite_out  <= MemWrite_in;
                RegWrite_out  <= RegWrite_in;
                MemToReg_out  <= MemToReg_in;
                ALUResult_out <= ALUResult_in;
                WriteData_out <= WriteData_in;
                Rd_out   <= Rd_in;
                jump_out      <= jump_in;
                branch_out    <= branch_in;
                zero_out      <= zero_in;
                branch_target_out <= branch_target_in;
            end if;
        end if;
    end process;
end Behavioral;
*/

/* Code of addr_trunc32to24:
library IEEE;
use IEEE.STD_LOGIC_1164.ALL;

entity addr_trunc32to24 is
    Port (
        addr_32 : in  STD_LOGIC_VECTOR(31 downto 0);
        addr_24 : out STD_LOGIC_VECTOR(23 downto 0)
    );
end addr_trunc32to24;

architecture Behavioral of addr_trunc32to24 is
begin
    -- Pass lower 24 bits
    addr_24 <= addr_32(23 downto 0);
end Behavioral;
*/

/* Code of MEM_WB_Pipeline:
library IEEE;
use IEEE.STD_LOGIC_1164.ALL;
use IEEE.NUMERIC_STD.ALL;

entity MEM_WB_Pipeline is
    Port (
        clk           : in  std_logic;
        reset         : in  std_logic;
        -- Control signals
        MemToReg_in   : in  std_logic;
        RegWrite_in   : in  std_logic;
        -- Data signals
        ReadData_in   : in  std_logic_vector(31 downto 0);
        ALUResult_in  : in  std_logic_vector(31 downto 0);
        Rd_in         : in  std_logic_vector(4 downto 0);

        -- Outputs to WB stage
        MemToReg_out  : out std_logic;
        RegWrite_out  : out std_logic;
        ALUResult_out : out std_logic_vector(31 downto 0);
        ReadData_out  : out std_logic_vector(31 downto 0);
        Rd_out   : out std_logic_vector(4 downto 0)
    );
end MEM_WB_Pipeline;

architecture Behavioral of MEM_WB_Pipeline is
begin
    process(clk, reset)
    begin
        if reset = '1' then
            RegWrite_out  <= '0';
            MemToReg_out  <= '0';
            ReadData_out  <= (others => '0');
            ALUResult_out <= (others => '0');
            Rd_out   <= (others => '0');
        elsif rising_edge(clk) then
            RegWrite_out  <= RegWrite_in;
            MemToReg_out  <= MemToReg_in;
            ReadData_out  <= ReadData_in;
            ALUResult_out <= ALUResult_in;
            Rd_out   <= Rd_in;
        end if;
    end process;
end Behavioral;
*/
