// Digital circuit teste.dig as structural Verilog
module teste (
  input  A,
  output B
);

  teste #(.applicationType("GHDL"), .CodeFile("C:\\Duds\\DuduClean\\ArquivosVScodePastaManual\\UFRJ\\periodo3\\ArqComp\\Pratica\\RISCV\\ArquivosVHDL\\teste1.vhdl")) u_teste (
    .a(A), .b(B));
endmodule
